# Fritzing sketch wiring (saved by Fritzing 0.9.2b)

parts:
  Part1 = Arduino Uno (Rev3)
  Part2 = SRF05 Ultrasonic Rangefinder
  Part3 = SRF05 Ultrasonic Rangefinder
  Part4 = SRF05 Ultrasonic Rangefinder
  Part5 = SRF05 Ultrasonic Rangefinder

nets:
  N1: Part1.A0, Part3.Trig
  N2: Part1.A1, Part3.Echo
  N3: Part1.A2, Part4.Trig
  N4: Part1.A3, Part4.Echo
  N5: Part1.A4/SDA, Part2.Echo
  N6: Part1.A5/SCL, Part2.Trig
  N7: Part1.D2, Part5.Trig
  N8: Part1.D3_PWM, Part5.Echo
